# Fritzing sketch BoomBox (saved by Fritzing 0.9.2b)
circuit board: 7.57688cm x 5.91863cm
perfboards: 1

parts:
  R13 = Resistor [tolerance=±5% resistance=22k package=THT]
  R2 = Resistor [tolerance=±5% resistance=470 package=THT]
  R3 = Trimmer Potentiometer [maximum_resistance=50kΩ package=THT]
  R4 = Resistor [tolerance=±5% resistance=56k package=THT]
  R5 = Resistor [tolerance=±5% resistance=1k package=THT]
  R6 = Resistor [tolerance=±5% resistance=1k package=THT]
  R7 = Resistor [tolerance=±5% resistance=470k package=THT]
  D5 = Zener Diode [part_number=1N4732A breakdown_voltage=5.1V package="300 mil [THT]"]
  U2 = TRANSISTOR_NPN_2 [part_number=BC547 package=to-92]
  R12 = Resistor [tolerance=±5% resistance=220k package=THT]
  C1 = Electrolytic Capacitor [capacitance=1µF voltage=20V package="100 mil [THT, electrolytic]"]
  U1 = 555 Timer [package="DIP8 [THT]"]
  IC2 = Dual Op-Amp [package=dip08]
  U4 = TRANSISTOR_NPN_2 [part_number=BC547 package=to-92]
  R14 = Resistor [tolerance=±5% resistance=10k package=THT]
  R15 = Resistor [tolerance=±5% resistance=10k package=THT]
  J2 = screw terminal, 3 pins
  J1 = screw terminal, 3 pins
  Q1 = Basic FET P-Channel [package="TO220 [THT]"]
  R17 = Resistor [tolerance=±5% resistance=220k package=THT]
  R18 = Resistor [tolerance=±5% resistance=1k package=THT]
  R19 = Resistor [tolerance=±5% resistance=1M package=THT]
  C4 = Electrolytic Capacitor [capacitance=4.7µF package="100 mil [THT, electrolytic]"]
  LED_Blink = screw terminal, 2 pins
  LED_PWR = screw terminal, 2 pins
  C6 = Electrolytic Capacitor [capacitance=4.7µF package="100 mil [THT, electrolytic]"]
  C7 = Ceramic Capacitor [capacitance=100nF package="200 mil [THT, multilayer]"]
  C5 = Ceramic Capacitor [capacitance=100nF package="200 mil [THT, multilayer]"]
  C8 = Electrolytic Capacitor [capacitance=1µF voltage=20V package="100 mil [THT, electrolytic]"]
  D6 = Diode [package=diode-1n4148]
  D7 = Schottky Diode [part_number=1N5817 breakdown_voltage=5.1V package="300 mil [THT]"]
  D8 = Schottky Diode [part_number=1N5817 breakdown_voltage=5.1V package="300 mil [THT]"]
  R20 = Resistor [tolerance=±5% resistance=47k package=THT]
  R21 = Resistor [tolerance=±5% resistance=47k package=THT]

nets:
  N1: R13.Pin_0, IC2.A_OUT, R17.Pin_1, R19.Pin_1
  N2: R13.Pin_1, U2.B
  N3: R2.Pin_0, R4.Pin_0, R12.Pin_0, IC2.A_V+, R17.Pin_0, C4.+, C5.1, D7.cathode
  N4: R2.Pin_1, D5.cathode, IC2.A_+IN, R19.Pin_0, R20.Pin_0
  N5: R3.leg1, R4.Pin_1
  N6: R3.wiper, IC2.A_-IN
  GND: R3.leg2, D5.anode, U2.E, IC2.A_V-, U4.E, J2.pin2, J1.pin2, C4.-, LED_PWR.pin1, C5.0, C8.-, R21.Pin_1
  N7: R5.Pin_0, LED_Blink.pin2
  N8: R5.Pin_1, U1.Output
  N9: R6.Pin_0, R7.Pin_1, U1.Discharge
  N10: R6.Pin_1, U1.Reset, U1.Vcc_Supply_Voltage, C6.+, C7.1, D8.cathode
  N11: R7.Pin_0, C1.+, U1.Trigger, U1.Threshold
  Blink: U2.C, C1.-, U1.Ground, LED_Blink.pin1, C6.-, C7.0
  N12: R12.Pin_1, IC2.B_OUT, J2.pin3
  N13: IC2.B_+IN, R20.Pin_1, R21.Pin_0
  N14: IC2.B_-IN, J1.pin3, D6.A
  N15: U4.C, R15.Pin_1, Q1.gate
  N16: U4.B, R14.Pin_1
  N17: R14.Pin_0, C8.+, D6.C
  12V: R15.Pin_0, J1.pin1, Q1.source
  VCC: J2.pin1, Q1.drain, R18.Pin_1, D7.anode, D8.anode
  N18: R18.Pin_0, LED_PWR.pin2

notes:
  BoomBox v0.5
  +  - SW
  +  - Mute
  AMP
  BAT
  -
